# Fritzing sketch Project 3 Control Servo via PWM (saved by Fritzing 0.9.3b)
breadboards: 1

parts:
  Mod2 = Raspberry Pi Pico
  J1 = Basic Servo

nets:
  N1: Mod2.pin_1, J1.pulse
  N2: Mod2.pin_3, Mod2.pin_8, Mod2.pin_13, Mod2.pin_18, Mod2.pin_23, Mod2.pin_28, Mod2.pin_33, Mod2.pin_38, Mod2.pin_42, J1.gnd
  N3: Mod2.pin_40, J1.vcc

custom parts:
  Raspberry Pi Pico: Raspberry Pi Pico. Based around the RP2040 microcontroller the Pico is a low cost microcontroller device bringing Raspberry Pi quality, cost, and easy of use to the microcontroller space. Jan 2021, Split part in to two versions: tht (this one) and SMD. This one will drill holes for a .1 in header in pcb to allow plugging in the module as well as providing pads to solder the module to the top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
